// Logisim project hack_architecture_CPU.circ as structural Verilog
module main (
);

  _16_bits_Hack_ALU u_16_bits_hack_alu_1 ();  // open: x, y, Output_8bits, zr, ng, zx, zy, nx, ny, f, no
endmodule

module _16_bits_Hack_ALU (
  input  zx,
  input  zy,
  input  nx,
  input  ny,
  input  f,
  input  no,
  input  [15:0] x,
  input  [15:0] y,
  output [15:0] Output_8bits,
  output zr,
  output ng
);

  wire [15:0] adder_1_out, and_1_out, multiplexer_16_bits_1_out_4, multiplexer_16_bits_2_out_4,
       multiplexer_16_bits_3_out_4, multiplexer_16_bits_4_out_4, multiplexer_16_bits_5_out_4, not_1_out,
       not_2_out, not_3_out;

  Multiplexer_16_bits multiplexer_16_bits_1 (.A(x), .B({16{1'b0}}), .Select(zx), .out_4(multiplexer_16_bits_1_out_4));
  assign not_1_out = ~multiplexer_16_bits_1_out_4;  // NOT_Gate not_1, 16 bits wide
  Multiplexer_16_bits multiplexer_16_bits_2 (.A(y), .B({16{1'b0}}), .Select(zy), .out_4(multiplexer_16_bits_2_out_4));
  assign not_2_out = ~multiplexer_16_bits_2_out_4;  // NOT_Gate not_2, 16 bits wide
  Multiplexer_16_bits multiplexer_16_bits_3 (
    .A(multiplexer_16_bits_1_out_4), .B(not_1_out), .Select(nx), .out_4(multiplexer_16_bits_3_out_4));
  Multiplexer_16_bits multiplexer_16_bits_4 (
    .A(multiplexer_16_bits_2_out_4), .B(not_2_out), .Select(ny), .out_4(multiplexer_16_bits_4_out_4));
  assign and_1_out = multiplexer_16_bits_3_out_4 & multiplexer_16_bits_4_out_4;  // AND_Gate and_1, 16 bits wide
  Adder #(.width(16)) adder_1 (
    .a(multiplexer_16_bits_3_out_4), .b(multiplexer_16_bits_4_out_4), .out(adder_1_out), .cin(1'b0));  // open: cout
  Multiplexer_16_bits multiplexer_16_bits_5 (
    .A(and_1_out), .B(adder_1_out), .Select(f), .out_4(multiplexer_16_bits_5_out_4));
  assign not_3_out = ~multiplexer_16_bits_5_out_4;  // NOT_Gate not_3, 16 bits wide
  Multiplexer_16_bits multiplexer_16_bits_6 (
    .A(multiplexer_16_bits_5_out_4), .B(not_3_out), .Select(no), .out_4(Output_8bits));
  nand nand_1 (zr, Output_8bits[0], Output_8bits[1], Output_8bits[2], Output_8bits[3], Output_8bits[4], Output_8bits[5], Output_8bits[6], Output_8bits[7], Output_8bits[8], Output_8bits[9], Output_8bits[10], Output_8bits[11], Output_8bits[12], Output_8bits[13], Output_8bits[14], Output_8bits[15]);
  buf buffer_1 (ng, Output_8bits[15]);
endmodule

module Multiplexer_16_bits (
  input  [15:0] A,
  input  [15:0] B,
  input  Select,
  output [15:0] out_4
);

  wire [15:0] and_1_out, and_2_out, not_1_out;

  assign not_1_out = ~{16{Select}};  // NOT_Gate not_1, 16 bits wide
  assign and_1_out = A & not_1_out;  // AND_Gate and_1, 16 bits wide
  assign and_2_out = {16{Select}} & B;  // AND_Gate and_2, 16 bits wide
  assign out_4 = and_1_out | and_2_out;  // OR_Gate or_1, 16 bits wide

  // Other names for the same wires on the sheet: sel[15:0] = {16{Select}}
endmodule

module _1_bit_register (
  input  In,
  input  Load,
  input  Clk,
  output out_4
);

  wire multiplexer_1_out;

  Multiplexer multiplexer_1 (.in0(out_4), .in1(In), .out(multiplexer_1_out), .sel(Load));  // open: en
  D_Flip_Flop d_ff_1 (.clk(Clk), .D(multiplexer_1_out), .Q(out_4));  // open: Qn, preset, en, reset
endmodule

module _16_bits_register (
  input  [15:0] in_1,
  input  Load,
  input  Clk,
  output [15:0] out_4,
  output [3:0] out_5
);

  _1_bit_register u_1_bit_register_1 (.In(in_1[0]), .out_4(out_4[0]), .Load(Load), .Clk(Clk));
  _1_bit_register u_1_bit_register_2 (.In(in_1[1]), .out_4(out_4[1]), .Load(Load), .Clk(Clk));
  _1_bit_register u_1_bit_register_3 (.In(in_1[2]), .out_4(out_4[2]), .Load(Load), .Clk(Clk));
  _1_bit_register u_1_bit_register_4 (.In(in_1[3]), .out_4(out_4[3]), .Load(Load), .Clk(Clk));
  _1_bit_register u_1_bit_register_5 (.In(in_1[4]), .out_4(out_4[4]), .Load(Load), .Clk(Clk));
  _1_bit_register u_1_bit_register_6 (.In(in_1[5]), .out_4(out_4[5]), .Load(Load), .Clk(Clk));
  _1_bit_register u_1_bit_register_7 (.In(in_1[6]), .out_4(out_4[6]), .Load(Load), .Clk(Clk));
  _1_bit_register u_1_bit_register_8 (.In(in_1[7]), .out_4(out_4[7]), .Load(Load), .Clk(Clk));
  _1_bit_register u_1_bit_register_9 (.In(in_1[8]), .out_4(out_4[8]), .Load(Load), .Clk(Clk));
  _1_bit_register u_1_bit_register_10 (.In(in_1[9]), .out_4(out_4[9]), .Load(Load), .Clk(Clk));
  _1_bit_register u_1_bit_register_11 (.In(in_1[10]), .out_4(out_4[10]), .Load(Load), .Clk(Clk));
  _1_bit_register u_1_bit_register_12 (.In(in_1[11]), .out_4(out_4[11]), .Load(Load), .Clk(Clk));
  _1_bit_register u_1_bit_register_13 (.In(in_1[12]), .out_4(out_4[12]), .Load(Load), .Clk(Clk));
  _1_bit_register u_1_bit_register_14 (.In(in_1[13]), .out_4(out_4[13]), .Load(Load), .Clk(Clk));
  _1_bit_register u_1_bit_register_15 (.In(in_1[14]), .out_4(out_4[14]), .Load(Load), .Clk(Clk));
  _1_bit_register u_1_bit_register_16 (.In(in_1[15]), .out_4(out_4[15]), .Load(Load), .Clk(Clk));

  assign out_5 = out_4[3:0];
endmodule

module Dmux8ways16bits (
  input  [2:0] Sel,
  input  [15:0] in_2,
  output [15:0] out_3,
  output [15:0] out_4,
  output [15:0] out_5,
  output [15:0] out_6,
  output [15:0] out_7,
  output [15:0] out_8,
  output [15:0] out_9,
  output [15:0] out_10
);

  wire [15:0] and_1_out, and_2_out, and_3_out, and_4_out, and_5_out, and_6_out, and_7_out, and_8_out,
       and_9_out, and_10_out, and_11_out, and_12_out, and_13_out, and_14_out, and_15_out, and_16_out,
       not_1_out, not_2_out, not_3_out;

  assign not_1_out = ~{16{Sel[2]}};  // NOT_Gate not_1, 16 bits wide
  assign not_2_out = ~{16{Sel[1]}};  // NOT_Gate not_2, 16 bits wide
  assign not_3_out = ~{16{Sel[0]}};  // NOT_Gate not_3, 16 bits wide
  assign and_1_out = in_2 & not_2_out;  // AND_Gate and_1, 16 bits wide
  assign and_2_out = in_2 & not_2_out;  // AND_Gate and_2, 16 bits wide
  assign and_3_out = in_2 & {16{Sel[1]}};  // AND_Gate and_3, 16 bits wide
  assign and_4_out = in_2 & not_1_out;  // AND_Gate and_4, 16 bits wide
  assign and_5_out = in_2 & {16{Sel[2]}};  // AND_Gate and_5, 16 bits wide
  assign and_6_out = in_2 & {16{Sel[2]}};  // AND_Gate and_6, 16 bits wide
  assign and_7_out = in_2 & {16{Sel[2]}};  // AND_Gate and_7, 16 bits wide
  assign and_8_out = in_2 & {16{Sel[2]}};  // AND_Gate and_8, 16 bits wide
  assign and_9_out = and_1_out & not_1_out;  // AND_Gate and_9, 16 bits wide
  assign and_10_out = and_2_out & not_1_out;  // AND_Gate and_10, 16 bits wide
  assign and_11_out = and_3_out & not_1_out;  // AND_Gate and_11, 16 bits wide
  assign and_12_out = and_4_out & {16{Sel[1]}};  // AND_Gate and_12, 16 bits wide
  assign and_13_out = and_5_out & not_2_out;  // AND_Gate and_13, 16 bits wide
  assign and_14_out = and_6_out & not_2_out;  // AND_Gate and_14, 16 bits wide
  assign and_15_out = and_7_out & {16{Sel[1]}};  // AND_Gate and_15, 16 bits wide
  assign and_16_out = and_8_out & {16{Sel[1]}};  // AND_Gate and_16, 16 bits wide
  assign out_3 = and_9_out & not_3_out;  // AND_Gate and_17, 16 bits wide
  assign out_4 = and_10_out & {16{Sel[0]}};  // AND_Gate and_18, 16 bits wide
  assign out_5 = and_11_out & not_3_out;  // AND_Gate and_19, 16 bits wide
  assign out_6 = and_12_out & {16{Sel[0]}};  // AND_Gate and_20, 16 bits wide
  assign out_7 = and_13_out & not_3_out;  // AND_Gate and_21, 16 bits wide
  assign out_8 = and_14_out & {16{Sel[0]}};  // AND_Gate and_22, 16 bits wide
  assign out_9 = and_15_out & not_3_out;  // AND_Gate and_23, 16 bits wide
  assign out_10 = and_16_out & {16{Sel[0]}};  // AND_Gate and_24, 16 bits wide

  // Other names for the same wires on the sheet: sel0_16[15:0] = {16{Sel[0]}}; sel1_16[15:0] = {16{Sel[1]}};
  //   sel2_16[15:0] = {16{Sel[2]}}
endmodule

module Mux8ways16bits (
  input  [15:0] in_1,
  input  [2:0] Sel,
  input  [15:0] in_3,
  input  [15:0] in_4,
  input  [15:0] in_5,
  input  [15:0] in_6,
  input  [15:0] in_7,
  input  [15:0] in_8,
  input  [15:0] in_9,
  output [15:0] out_10
);

  wire [15:0] and_1_out, and_2_out, and_3_out, and_4_out, and_5_out, and_6_out, and_7_out, and_8_out,
       not_1_out, not_2_out, not_3_out, or_1_out, or_2_out, or_3_out, or_4_out, or_5_out, or_6_out;

  assign not_1_out = ~{16{Sel[2]}};  // NOT_Gate not_1, 16 bits wide
  assign not_2_out = ~{16{Sel[0]}};  // NOT_Gate not_2, 16 bits wide
  assign not_3_out = ~{16{Sel[1]}};  // NOT_Gate not_3, 16 bits wide
  assign and_1_out = in_1 & not_1_out & not_3_out & not_2_out;  // AND_Gate and_1, 16 bits wide
  assign and_2_out = in_3 & not_1_out & not_3_out & {16{Sel[0]}};  // AND_Gate and_2, 16 bits wide
  assign and_3_out = in_4 & not_1_out & {16{Sel[1]}} & not_2_out;  // AND_Gate and_3, 16 bits wide
  assign and_4_out = in_5 & not_1_out & {16{Sel[1]}} & {16{Sel[0]}};  // AND_Gate and_4, 16 bits wide
  assign and_5_out = in_6 & {16{Sel[2]}} & not_3_out & not_2_out;  // AND_Gate and_5, 16 bits wide
  assign and_6_out = in_7 & {16{Sel[2]}} & not_3_out & {16{Sel[0]}};  // AND_Gate and_6, 16 bits wide
  assign and_7_out = in_8 & {16{Sel[2]}} & {16{Sel[1]}} & not_2_out;  // AND_Gate and_7, 16 bits wide
  assign and_8_out = in_9 & {16{Sel[2]}} & {16{Sel[1]}} & {16{Sel[0]}};  // AND_Gate and_8, 16 bits wide
  assign or_1_out = and_1_out | and_2_out;  // OR_Gate or_1, 16 bits wide
  assign or_2_out = and_3_out | and_4_out;  // OR_Gate or_2, 16 bits wide
  assign or_3_out = and_5_out | and_6_out;  // OR_Gate or_3, 16 bits wide
  assign or_4_out = and_7_out | and_8_out;  // OR_Gate or_4, 16 bits wide
  assign or_5_out = or_1_out | or_2_out;  // OR_Gate or_5, 16 bits wide
  assign or_6_out = or_3_out | or_4_out;  // OR_Gate or_6, 16 bits wide
  assign out_10 = or_5_out | or_6_out;  // OR_Gate or_7, 16 bits wide

  // Other names for the same wires on the sheet: sel0_16[15:0] = {16{Sel[0]}}; sel1_16[15:0] = {16{Sel[1]}};
  //   sel2_16[15:0] = {16{Sel[2]}}
endmodule

module _128kb_Ram (
  input  [15:0] In,
  input  [2:0] Addr,
  input  Load,
  input  Clk,
  output [15:0] out_5
);

  wire loadR1, loadR2, loadR3, loadR4, loadR5, loadR6, loadR7, loadR8;
  wire [3:0] n16_bits_register_1_out_5, n16_bits_register_2_out_5, n16_bits_register_3_out_5,
       n16_bits_register_4_out_5, n16_bits_register_5_out_5, n16_bits_register_6_out_5,
       n16_bits_register_7_out_5, n16_bits_register_8_out_5;
  wire [15:0] dmux8ways16bits_1_out_3, dmux8ways16bits_1_out_4, dmux8ways16bits_1_out_5,
       dmux8ways16bits_1_out_6, dmux8ways16bits_1_out_7, dmux8ways16bits_1_out_8, dmux8ways16bits_1_out_9,
       dmux8ways16bits_1_out_10, n16_bits_register_1_out_4, n16_bits_register_2_out_4,
       n16_bits_register_3_out_4, n16_bits_register_4_out_4, n16_bits_register_5_out_4,
       n16_bits_register_6_out_4, n16_bits_register_7_out_4, n16_bits_register_8_out_4;

  Dmux8ways16bits dmux8ways16bits_1 (
    .Sel(Addr), .in_2(In), .out_3(dmux8ways16bits_1_out_3), .out_4(dmux8ways16bits_1_out_4),
    .out_5(dmux8ways16bits_1_out_5), .out_6(dmux8ways16bits_1_out_6), .out_7(dmux8ways16bits_1_out_7),
    .out_8(dmux8ways16bits_1_out_8), .out_9(dmux8ways16bits_1_out_9), .out_10(dmux8ways16bits_1_out_10));
  Demultiplexer #(.select(3), .enable("false")) demultiplexer_1 (
    .out0(loadR1), .out1(loadR2), .out2(loadR3), .out3(loadR4), .out4(loadR5), .out5(loadR6), .out6(loadR7),
    .out7(loadR8), .in(Load), .sel(Addr));
  Hex_Digit_Display hex_digit_display_1 (.value(n16_bits_register_1_out_5));  // open: dp
  _16_bits_register u_16_bits_register_1 (
    .in_1(dmux8ways16bits_1_out_3), .out_4(n16_bits_register_1_out_4), .Load(loadR1), .Clk(Clk),
    .out_5(n16_bits_register_1_out_5));
  _16_bits_register u_16_bits_register_2 (
    .in_1(dmux8ways16bits_1_out_4), .out_4(n16_bits_register_2_out_4), .Load(loadR2), .Clk(Clk),
    .out_5(n16_bits_register_2_out_5));
  _16_bits_register u_16_bits_register_3 (
    .in_1(dmux8ways16bits_1_out_5), .out_4(n16_bits_register_3_out_4), .Load(loadR3), .Clk(Clk),
    .out_5(n16_bits_register_3_out_5));
  _16_bits_register u_16_bits_register_4 (
    .in_1(dmux8ways16bits_1_out_6), .out_4(n16_bits_register_4_out_4), .Load(loadR4), .Clk(Clk),
    .out_5(n16_bits_register_4_out_5));
  _16_bits_register u_16_bits_register_5 (
    .in_1(dmux8ways16bits_1_out_7), .out_4(n16_bits_register_5_out_4), .Load(loadR5), .Clk(Clk),
    .out_5(n16_bits_register_5_out_5));
  _16_bits_register u_16_bits_register_6 (
    .in_1(dmux8ways16bits_1_out_8), .out_4(n16_bits_register_6_out_4), .Load(loadR6), .Clk(Clk),
    .out_5(n16_bits_register_6_out_5));
  _16_bits_register u_16_bits_register_7 (
    .in_1(dmux8ways16bits_1_out_9), .out_4(n16_bits_register_7_out_4), .Load(loadR7), .Clk(Clk),
    .out_5(n16_bits_register_7_out_5));
  _16_bits_register u_16_bits_register_8 (
    .in_1(dmux8ways16bits_1_out_10), .out_4(n16_bits_register_8_out_4), .Load(loadR8), .Clk(Clk),
    .out_5(n16_bits_register_8_out_5));
  Hex_Digit_Display hex_digit_display_2 (.value(n16_bits_register_3_out_5));  // open: dp
  Hex_Digit_Display hex_digit_display_3 (.value(n16_bits_register_2_out_5));  // open: dp
  Hex_Digit_Display hex_digit_display_4 (.value(n16_bits_register_5_out_5));  // open: dp
  Hex_Digit_Display hex_digit_display_5 (.value(n16_bits_register_4_out_5));  // open: dp
  Hex_Digit_Display hex_digit_display_6 (.value(n16_bits_register_6_out_5));  // open: dp
  Hex_Digit_Display hex_digit_display_7 (.value(n16_bits_register_7_out_5));  // open: dp
  Hex_Digit_Display hex_digit_display_8 (.value(n16_bits_register_8_out_5));  // open: dp
  Mux8ways16bits mux8ways16bits_1 (
    .in_1(n16_bits_register_1_out_4), .Sel(Addr), .in_3(n16_bits_register_2_out_4),
    .in_4(n16_bits_register_3_out_4), .in_5(n16_bits_register_4_out_4), .in_6(n16_bits_register_5_out_4),
    .in_7(n16_bits_register_6_out_4), .in_8(n16_bits_register_7_out_4), .in_9(n16_bits_register_8_out_4),
    .out_10(out_5));
endmodule
